# Fritzing sketch lucas_gokart (saved by Fritzing 0.9.6b)

parts:
  Mod1 = Nano-V3-0-IO-Expansion-Adapter
  Mod2 = KY-003 Hall Magnetic Sensor Module [package="Breakout board"]
  Mod3 = KY-003 Hall Magnetic Sensor Module [package="Breakout board"]
  M1 = BTS7960
  M2 = BTS7960
  M3 = DC Motor
  Part1 = Arduino Nano (Rev3.0)
  Part2 = Thumb Joystick
  M4 = DC Motor
  BAT1 = 12 battery [package=battery]
  BAT2 = 12 battery [package=battery]

nets:
  VCC: Mod1.VCC, Part1.5V, Part2.VCC
  GND: Mod1.GND, Mod3.-, Part1.GND, Part2.GND
  VIN: Mod1.VIN, Part1.VIN
  N1: Mod1.A0, Part1.A0, Part2.VERT
  N2: Mod1.A1, Part1.A1, Part2.HORZ
  N3: Mod1.D13/SCK, Part1.D13/SCK
  N4: Mod1.NC, Part1.3V3
  N5: Mod1.AREF, Part1.AREF
  N6: Mod1.A2, Part1.A2
  N7: Mod1.A3, Part1.A3
  N8: Mod1.A4/SDA, Part1.A4
  N9: Mod1.A5/SCL, Part1.A5
  N10: Mod1.A6, Part1.A6
  N11: Mod1.A7, Part1.A7
  N12: Mod1.RST, Part1.RESET
  N13: Mod1.D12/MISO, Part1.D12/MISO
  N14: Mod1.D11_PWM/MOSI, Part1.D11/MOSI
  N15: Mod1.D10_PWM/SS, M1.pin1, Part1.D10
  N16: Mod1.D9_PWM, M1.pin2, Part1.D9
  N17: Mod1.D8, M1.pin3, M1.pin4, Part1.D8
  N18: Mod1.D7, Part1.D7
  N19: Mod1.D6_PWM, M2.pin1, Part1.D6
  N20: Mod1.D5_PWM, M2.pin2, Part1.D5
  N21: Mod1.D4, M2.pin3, M2.pin4, Part1.D4
  N22: Mod1.D3_PWM, Mod3.S, Part1.D3
  N23: Mod1.D2, Mod2.S, Part1.D2
  N24: Mod1.D0/RX#64, Mod1.D1/TX#79, Mod1.D1/TX#83, Mod2.-, Part1.D0/RX
  VIN_2: Mod1.D1/TX#65, Mod1.D0/RX#78, Mod1.D0/RX#80, Mod2.Vin, Mod3.Vin, Part1.D1/TX
  N25: M1.pin9, M3.pin_2
  N26: M1.pin10, M3.pin_1
  N27: M1.pin11, M2.pin10, BAT2.-
  N28: M1.pin12, M2.pin9, BAT1.+
  N29: M2.pin11, M4.pin_2
  N30: M2.pin12, M4.pin_1
  N31: BAT1.-, BAT2.+

notes:
  Left Motor Hall Sensor
  Right Motor Hall Sensor
  24V Brushed DC Motor
  BTS7960 43A Motor Driver
  Arduino Nano + Expansion Board
  Joystick Controller

custom parts:
  Nano-V3-0-IO-Expansion-Adapter: Nano V3.0 IO Expansion Adapter Shield. Note pcb view has been supressed as not useful. You can drag a Nano over the Nano connectors and it will connect and appear in schematic (although at present due to a bug, routing will not show as complete in breadboard).
  KY-003 Hall Magnetic Sensor Module: KEYES KY-003 Arduino Hall Magnetic Sensor Module is a switch that will turn on/off in the presence of a magnetic field.
  BTS7960: BTS7960 43A Peak Power H-Bridge PWM Motor Driver
  12 battery: 12V lead acid type battery, like the Husqvarna YTH2448 12V 35AH battery. This is the mini version 1/4 the size of the actual battery to be closer to typical breadboard parts (around 2in wide rathher than 7in). The pads in pcb are sized to accomidate up to 14ga wire (as these batterys will deliver high currents.)
